// Logisim project Pipelined Processor Design.circ as structural Verilog: 3 circuits, main circuit main
module main (
  input  [1:0] PCSrc,
  input  in_2,
  input  in_3,
  input  in_4,
  input  WBdata,
  output [7:0] out_6
);

  wire and_1_out, and_2_out, clock_1_out, comparator_1_gt, decoder_1_out1, decoder_1_out2, decoder_1_out4,
       not_1_out, not_2_out, or_1_out, or_2_out;
  wire [5:0] ram_1_data;
  wire [7:0] bit_extender_2_out, bit_extender_3_out, multiplexer_2_out, multiplexer_3_out, multiplexer_4_out,
       ram_2_data, registerfile_1_busa, registerfile_1_busb;
  wire [10:0] decoder_1_out5;
  wire [11:0] adder_1_out, adder_2_out, bit_extender_1_out, multiplexer_1_out, PC_q;
  wire [11:6] ram_1_data_2;
  wire [15:12] ram_1_data_3;

  and and_1 (and_1_out, decoder_1_out1, ram_1_data[5], ram_1_data[4], ram_1_data[3], ram_1_data[2], ram_1_data[1], ram_1_data[0]);
  assign bit_extender_1_out = {{4{1'b0}}, bit_extender_2_out};  // Bit_Extender bit_extender_1
  and and_2 (and_2_out, ram_1_data[2], ram_1_data[1], not_1_out);
  not not_1 (not_1_out, ram_1_data[0]);
  Adder #(.width(12)) adder_1 (.a(PC_q), .b(12'h1), .out(adder_1_out));  // open: cin, cout
  Adder #(.width(12)) adder_2 (.a(adder_1_out), .b(bit_extender_1_out), .out(adder_2_out));  // open: cin, cout
  Multiplexer #(.select(2), .width(12), .enable("false")) multiplexer_1 (
    .in0(adder_1_out), .in1({ram_1_data_2, ram_1_data}), .in3(adder_2_out), .out(multiplexer_1_out),
    .sel(PCSrc));  // open: in2
  Register #(.width(12)) PC (.D(multiplexer_1_out), .en(1'b1), .Q(PC_q), .clk(clock_1_out));  // open: clr
  Clock clock_1 (.out(clock_1_out));
  Decoder #(.select(4), .enable("false")) decoder_1 (
    .out1(decoder_1_out1), .out2(decoder_1_out2), .out3(decoder_1_out2), .out4(decoder_1_out4),
    .out5(decoder_1_out5[0]), .out6(decoder_1_out5[1]), .out7(decoder_1_out5[2]), .out8(decoder_1_out5[3]),
    .out9(decoder_1_out5[4]), .out10(decoder_1_out5[5]), .out11(decoder_1_out5[6]),
    .out12(decoder_1_out5[7]), .out13(decoder_1_out5[8]), .out14(decoder_1_out5[9]),
    .out15(decoder_1_out5[10]), .sel(ram_1_data_3));  // open: out0
  RegisterFile registerfile_1 (
    .BusW(multiplexer_4_out), .Clock(clock_1_out), .RegWrite(not_2_out), .RA(ram_1_data[5:3]),
    .RB(ram_1_data_2[8:6]), .RW(ram_1_data_2[11:9]), .BusA(registerfile_1_busa), .BusB(registerfile_1_busb));
  not not_2 (not_2_out, comparator_1_gt);
  Comparator #(.width(11), .mode("unsigned")) comparator_1 (
    .a(decoder_1_out5), .b({11{1'b0}}), .gt(comparator_1_gt));  // open: eq, lt
  RAM #(.addrWidth(12), .dataWidth(16)) ram_1 (
    .addr(PC_q), .data({ram_1_data_3, ram_1_data_2, ram_1_data}), .clk(clock_1_out));  // open: sel, ld, clr
  Multiplexer #(.width(8), .enable("false")) multiplexer_2 (
    .in0(bit_extender_2_out), .in1(bit_extender_3_out), .out(multiplexer_2_out), .sel(or_1_out));
  buf or_1 (or_1_out, decoder_1_out2);  // OR_Gate
  assign bit_extender_2_out = {{2{ram_1_data[5]}}, ram_1_data};  // Bit_Extender bit_extender_2
  assign bit_extender_3_out = {{2{1'b0}}, ram_1_data};  // Bit_Extender bit_extender_3
  Multiplexer #(.width(8), .enable("false")) multiplexer_3 (
    .in0(registerfile_1_busb), .in1(multiplexer_2_out), .out(multiplexer_3_out), .sel(or_2_out));
  or or_2 (or_2_out, decoder_1_out4, decoder_1_out2);
  ALU alu_1 (.Op(ram_1_data_3), .func(ram_1_data[2:0]), .Rt(registerfile_1_busa), .Rs(multiplexer_3_out), .Rd(out_6));
  Multiplexer #(.width(8), .enable("false")) multiplexer_4 (
    .in0(out_6), .in1(ram_2_data), .out(multiplexer_4_out), .sel(WBdata));
  RAM #(.bus("separate")) ram_2 (
    .addr(out_6), .din(registerfile_1_busb), .data(ram_2_data), .str(in_2), .clk(clock_1_out), .ld(in_3),
    .clr(in_4));  // open: sel

  // Notes on the sheet:
  //   JALR
  //   JR
  //   func
  //   Rt
  //   RegWrite
  //   Instructions Memory
  //   Signed Or Zero
  //   SW
  //   LW
  //   BNE
  //   BEQ
  //   BGT
  //   BGE
  //   BLT
  //   BLE
  //   Jump
  //   Jump and Link
  //   I-Type
  //   R-type
  //   Load Upper Immediate
  //   J-type
  //   ALUSrc
  //   ALUop
  //   DataMemory
endmodule

module RegisterFile (
  input  [2:0] RB,
  input  [7:0] BusW,
  input  [2:0] RA,
  input  Clock,
  input  RegWrite,
  input  [2:0] RW,
  output [7:0] BusB,
  output [7:0] BusA
);

  wire _1_out, _2_out, _3_out, _4_out, _5_out, _6_out, _7_out, decoder_1_out1, decoder_1_out2,
       decoder_1_out3, decoder_1_out4, decoder_1_out5, decoder_1_out6, decoder_1_out7, decoder_2_out0,
       decoder_2_out1, decoder_2_out2, decoder_2_out3, decoder_2_out4, decoder_2_out5, decoder_2_out6,
       decoder_2_out7, decoder_3_out0, decoder_3_out1, decoder_3_out2, decoder_3_out3, decoder_3_out4,
       decoder_3_out5, decoder_3_out6, decoder_3_out7;
  wire [7:0] R1_q, R2_q, R3_q, R4_q, R5_q, R6_q, R7_q;

  Decoder #(.select(3)) decoder_1 (
    .out1(decoder_1_out1), .out2(decoder_1_out2), .out3(decoder_1_out3), .out4(decoder_1_out4),
    .out5(decoder_1_out5), .out6(decoder_1_out6), .out7(decoder_1_out7), .sel(RW), .en(1'b1));  // open: out0
  and _1 (_1_out, decoder_1_out1, RegWrite);
  and _2 (_2_out, decoder_1_out2, RegWrite);
  and _3 (_3_out, decoder_1_out3, RegWrite);
  and _4 (_4_out, decoder_1_out4, RegWrite);
  and _5 (_5_out, decoder_1_out5, RegWrite);
  and _6 (_6_out, decoder_1_out6, RegWrite);
  and _7 (_7_out, decoder_1_out7, RegWrite);
  Register R1 (.D(BusW), .en(_1_out), .Q(R1_q), .clk(Clock));  // open: clr
  Register R2 (.D(BusW), .en(_2_out), .Q(R2_q), .clk(Clock));  // open: clr
  Register R3 (.D(BusW), .en(_3_out), .Q(R3_q), .clk(Clock));  // open: clr
  Register R4 (.D(BusW), .en(_4_out), .Q(R4_q), .clk(Clock));  // open: clr
  Register R5 (.D(BusW), .en(_5_out), .Q(R5_q), .clk(Clock));  // open: clr
  Register R6 (.D(BusW), .en(_6_out), .Q(R6_q), .clk(Clock));  // open: clr
  Register R7 (.D(BusW), .en(_7_out), .Q(R7_q), .clk(Clock));  // open: clr
  assign BusA = decoder_2_out0 ? {8{1'b0}} : 8'bz;  // Controlled_Buffer controlled_buffer_1
  assign BusA = decoder_2_out2 ? R2_q : 8'bz;  // Controlled_Buffer controlled_buffer_2
  assign BusA = decoder_2_out1 ? R1_q : 8'bz;  // Controlled_Buffer controlled_buffer_3
  Decoder #(.select(3)) decoder_2 (
    .out0(decoder_2_out0), .out1(decoder_2_out1), .out2(decoder_2_out2), .out3(decoder_2_out3),
    .out4(decoder_2_out4), .out5(decoder_2_out5), .out6(decoder_2_out6), .out7(decoder_2_out7), .sel(RA),
    .en(1'b1));
  assign BusA = decoder_2_out6 ? R6_q : 8'bz;  // Controlled_Buffer controlled_buffer_4
  assign BusA = decoder_2_out5 ? R5_q : 8'bz;  // Controlled_Buffer controlled_buffer_5
  assign BusA = decoder_2_out4 ? R4_q : 8'bz;  // Controlled_Buffer controlled_buffer_6
  assign BusA = decoder_2_out3 ? R3_q : 8'bz;  // Controlled_Buffer controlled_buffer_7
  assign BusA = decoder_2_out7 ? R7_q : 8'bz;  // Controlled_Buffer controlled_buffer_8
  assign BusB = decoder_3_out0 ? {8{1'b0}} : 8'bz;  // Controlled_Buffer controlled_buffer_9
  assign BusB = decoder_3_out3 ? R3_q : 8'bz;  // Controlled_Buffer controlled_buffer_10
  assign BusB = decoder_3_out2 ? R2_q : 8'bz;  // Controlled_Buffer controlled_buffer_11
  assign BusB = decoder_3_out1 ? R1_q : 8'bz;  // Controlled_Buffer controlled_buffer_12
  Decoder #(.select(3)) decoder_3 (
    .out0(decoder_3_out0), .out1(decoder_3_out1), .out2(decoder_3_out2), .out3(decoder_3_out3),
    .out4(decoder_3_out4), .out5(decoder_3_out5), .out6(decoder_3_out6), .out7(decoder_3_out7), .sel(RB),
    .en(1'b1));
  assign BusB = decoder_3_out7 ? R7_q : 8'bz;  // Controlled_Buffer controlled_buffer_13
  assign BusB = decoder_3_out6 ? R6_q : 8'bz;  // Controlled_Buffer controlled_buffer_14
  assign BusB = decoder_3_out5 ? R5_q : 8'bz;  // Controlled_Buffer controlled_buffer_15
  assign BusB = decoder_3_out4 ? R4_q : 8'bz;  // Controlled_Buffer controlled_buffer_16

  // Notes on the sheet:
  //   STAGE 1
  //   STAGE 2
endmodule

module ALU (
  input  [3:0] Op,
  input  [2:0] func,
  input  [7:0] Rs,
  input  [7:0] Rt,
  output [7:0] Rd
);

  wire comparator_1_eq, comparator_1_gt, comparator_2_eq, comparator_2_gt, comparator_3_eq, not_2_out,
       not_3_out, not_4_out, or_2_out, undriven;
  wire [7:0] adder_1_out, adder_2_out, and_1_out, and_2_out, bit_extender_1_out, bit_extender_2_out,
       bit_extender_3_out, bit_extender_4_out, bit_extender_5_out, bit_extender_6_out, bit_extender_7_out,
       bit_extender_8_out, bit_extender_9_out, multiplexer_1_out, multiplexer_2_out, not_1_out, not_5_out,
       or_1_out, shifter_1_out, shifter_2_out, shifter_3_out, shifter_4_out, subtractor_1_out, xor_1_out;

  assign or_1_out = Rs | Rt;  // OR_Gate or_1, 8 bits wide
  assign xor_1_out = Rt ^ Rs;  // XOR_Gate xor_1, 8 bits wide
  assign and_1_out = Rt & Rs;  // AND_Gate and_1, 8 bits wide
  Adder adder_1 (.a(Rt), .b(Rs), .out(adder_1_out));  // open: cin, cout
  Subtractor subtractor_1 (.a(Rt), .b(Rs), .out(subtractor_1_out));  // open: bin, bout
  Comparator comparator_1 (.a(Rt), .b(Rs), .gt(comparator_1_gt), .eq(comparator_1_eq));  // open: lt
  Comparator #(.mode("unsigned")) comparator_2 (
    .a(Rt), .b(Rt), .gt(comparator_2_gt), .eq(comparator_2_eq));  // open: lt
  Shifter shifter_1 (.in(Rs), .\dist (Rt[2:0]), .out(shifter_1_out));
  Shifter #(.shift("ar")) shifter_2 (.in(Rs), .\dist (Rt[2:0]), .out(shifter_2_out));
  or or_2 (or_2_out, comparator_1_gt, comparator_1_eq);
  // OR_Gate or_3 has open pins: in1=comparator_2_eq, out=open
  Shifter #(.shift("lr")) shifter_3 (.in(Rs), .\dist (Rt[2:0]), .out(shifter_3_out));
  Shifter #(.shift("rr")) shifter_4 (.in(Rs), .\dist (Rt[2:0]), .out(shifter_4_out));
  Comparator #(.mode("unsigned")) comparator_3 (.a(Rs), .b({8{1'b0}}), .eq(comparator_3_eq));  // open: gt, lt
  assign not_1_out = ~and_1_out;  // NOT_Gate not_1, 8 bits wide
  assign bit_extender_1_out = {{7{1'b0}}, or_2_out};  // Bit_Extender bit_extender_1
  assign bit_extender_2_out = {{7{1'b0}}, undriven};  // Bit_Extender bit_extender_2
  assign bit_extender_3_out = {{7{1'b1}}, comparator_3_eq};  // Bit_Extender bit_extender_3
  assign and_2_out = bit_extender_3_out & Rt;  // AND_Gate and_2, 8 bits wide
  Multiplexer #(.select(3), .width(8), .enable("false")) multiplexer_1 (
    .in0(or_1_out), .in1(not_1_out), .in2(xor_1_out), .in4(adder_1_out), .in5(subtractor_1_out),
    .in6(bit_extender_1_out), .in7(bit_extender_2_out), .out(multiplexer_1_out), .sel(func));  // open: in3
  not not_2 (not_2_out, comparator_2_eq);
  not not_3 (not_3_out, or_2_out);
  not not_4 (not_4_out, comparator_1_gt);
  Multiplexer #(.select(3), .width(8), .enable("false")) multiplexer_2 (
    .in0(shifter_1_out), .in1(shifter_3_out), .in2(shifter_2_out), .in4(shifter_4_out), .in5(and_2_out),
    .in7(not_5_out), .out(multiplexer_2_out), .sel(func));  // open: in3, in6
  assign not_5_out = ~and_2_out;  // NOT_Gate not_5, 8 bits wide
  assign bit_extender_4_out = {{7{1'b0}}, not_2_out};  // Bit_Extender bit_extender_4
  assign bit_extender_5_out = {{7{1'b0}}, comparator_2_eq};  // Bit_Extender bit_extender_5
  assign bit_extender_6_out = {{7{1'b0}}, comparator_1_gt};  // Bit_Extender bit_extender_6
  assign bit_extender_7_out = {{7{1'b0}}, or_2_out};  // Bit_Extender bit_extender_7
  assign bit_extender_8_out = {{7{1'b0}}, not_3_out};  // Bit_Extender bit_extender_8
  assign bit_extender_9_out = {{7{1'b0}}, not_4_out};  // Bit_Extender bit_extender_9
  Adder adder_2 (.a(Rs), .b(Rt), .out(adder_2_out));  // open: cin, cout
  Multiplexer #(.select(4), .width(8), .enable("false")) multiplexer_3 (
    .in0(multiplexer_1_out), .in1(multiplexer_2_out), .in2(and_1_out), .in3(or_1_out), .in4(adder_1_out),
    .in5(adder_2_out), .in6(adder_2_out), .in7(bit_extender_4_out), .in8(bit_extender_5_out),
    .in9(bit_extender_6_out), .in10(bit_extender_7_out), .in11(bit_extender_8_out),
    .in12(bit_extender_9_out), .out(Rd), .sel(Op));  // open: in13, in14, in15

  // Notes on the sheet:
  //   ALU For Op = 0000
  //   OR 
  //   NAND
  //   XOR
  //   ADD
  //   SUB
  //   SGE
  //   SGEU
  //   ALU For Op = 0001
  //   SLL
  //   SRL
  //   SRA
  //   ROR
  //   MOVZ MOVN
  //   Signed
endmodule
